// Logisim project lab06part1.circ as structural Verilog: 1 circuit, main circuit main
module main (
  input  A,
  input  B,
  input  C_in,
  output out_4,
  output out_5
);

  wire _01_out, _02_out, _04_out, A1_out, A2_out, A3_out, A4_out, A5_out, A6_out, A7_out, A8_out, A9_out,
       A10_out, A11_out, not_1_out, not_2_out, not_3_out;

  not not_1 (not_1_out, A);
  not not_2 (not_2_out, B);
  not not_3 (not_3_out, C_in);
  and A1 (A1_out, not_1_out, not_2_out);
  and A2 (A2_out, A1_out, C_in);
  and A3 (A3_out, not_1_out, B);
  and A4 (A4_out, A3_out, not_3_out);
  and A5 (A5_out, A, not_2_out);
  and A6 (A6_out, A5_out, not_3_out);
  and A7 (A7_out, A, B);
  and A8 (A8_out, A7_out, C_in);
  and A9 (A9_out, C_in, A);
  and A10 (A10_out, C_in, B);
  and A11 (A11_out, B, A);
  or _01 (_01_out, A2_out, A4_out);
  or _02 (_02_out, A6_out, A8_out);
  or _04 (_04_out, A9_out, A10_out);
  or _05 (out_5, _04_out, A11_out);
  or _03 (out_4, _01_out, _02_out);
endmodule
