// Logisim project lab08.circ as structural Verilog: 3 circuits, main circuit main
module main (
  input  [3:0] in_1,
  input  [7:0] in_2,
  input  [7:0] in_3,
  output out_4,
  output [7:0] out_5,
  output out_6
);

  _8BitALU u_8bitalu_1 (.Inputs(in_1), .in_2(in_2), .b(in_3), .out_4(out_5), .Zero(out_4), .Overflow(out_6));

  // Notes on the sheet:
  //   0 = and
  //   1 = or
  //   10 = Addition
  //   11 = Less
endmodule

module _1bitALU (
  input  [1:0] OPERATION,
  input  A_INVERT,
  input  BINVERT,
  input  CARRY_IN,
  input  A,
  input  B,
  input  LESS,
  output RESULT,
  output CARRYOUT,
  output SET
);

  wire and_1_out, multiplexer_1_out, multiplexer_2_out, not_1_out, not_2_out, or_1_out;

  not not_1 (not_1_out, A);
  not not_2 (not_2_out, B);
  Multiplexer multiplexer_1 (.in0(A), .in1(not_1_out), .out(multiplexer_1_out), .sel(A_INVERT));  // open: en
  Multiplexer multiplexer_2 (.in0(B), .in1(not_2_out), .out(multiplexer_2_out), .sel(BINVERT));  // open: en
  or or_1 (or_1_out, multiplexer_1_out, multiplexer_2_out);
  and and_1 (and_1_out, multiplexer_1_out, multiplexer_2_out);
  Adder #(.width(1)) adder_1 (.a(multiplexer_1_out), .b(multiplexer_2_out), .out(SET), .cin(CARRY_IN), .cout(CARRYOUT));
  Multiplexer #(.select(2)) multiplexer_3 (
    .in0(and_1_out), .in1(or_1_out), .in2(SET), .in3(LESS), .out(RESULT), .sel(OPERATION));  // open: en
endmodule

module _8BitALU (
  input  [3:0] Inputs,
  input  [7:0] in_2,
  input  [7:0] b,
  output [7:0] out_4,
  output Zero,
  output Overflow
);

  wire n1bitalu_1_carryout, n1bitalu_2_carryout, n1bitalu_3_carryout, n1bitalu_4_carryout,
       n1bitalu_5_carryout, n1bitalu_6_carryout, n1bitalu_7_carryout, n1bitalu_8_set, or_1_out;

  _1bitALU u_1bitalu_1 (
    .A(in_2[0]), .B(b[0]), .LESS(n1bitalu_8_set), .A_INVERT(Inputs[3]), .BINVERT(Inputs[2]),
    .CARRY_IN(Inputs[2]), .OPERATION(Inputs[1:0]), .CARRYOUT(n1bitalu_1_carryout), .RESULT(out_4[0]));  // open: SET
  _1bitALU u_1bitalu_2 (
    .A(in_2[1]), .B(b[1]), .LESS(1'b0), .A_INVERT(Inputs[3]), .BINVERT(Inputs[2]),
    .CARRY_IN(n1bitalu_1_carryout), .OPERATION(Inputs[1:0]), .CARRYOUT(n1bitalu_2_carryout), .RESULT(out_4[1]));  // open: SET
  _1bitALU u_1bitalu_3 (
    .A(in_2[2]), .B(b[2]), .LESS(1'b0), .A_INVERT(Inputs[3]), .BINVERT(Inputs[2]),
    .CARRY_IN(n1bitalu_2_carryout), .OPERATION(Inputs[1:0]), .CARRYOUT(n1bitalu_3_carryout), .RESULT(out_4[2]));  // open: SET
  _1bitALU u_1bitalu_4 (
    .A(in_2[3]), .B(b[3]), .LESS(1'b0), .A_INVERT(Inputs[3]), .BINVERT(Inputs[2]),
    .CARRY_IN(n1bitalu_3_carryout), .OPERATION(Inputs[1:0]), .CARRYOUT(n1bitalu_4_carryout), .RESULT(out_4[3]));  // open: SET
  _1bitALU u_1bitalu_5 (
    .A(in_2[4]), .B(b[4]), .LESS(1'b0), .A_INVERT(Inputs[3]), .BINVERT(Inputs[2]),
    .CARRY_IN(n1bitalu_4_carryout), .OPERATION(Inputs[1:0]), .CARRYOUT(n1bitalu_5_carryout), .RESULT(out_4[4]));  // open: SET
  _1bitALU u_1bitalu_6 (
    .A(in_2[5]), .B(b[5]), .LESS(1'b0), .A_INVERT(Inputs[3]), .BINVERT(Inputs[2]),
    .CARRY_IN(n1bitalu_5_carryout), .OPERATION(Inputs[1:0]), .CARRYOUT(n1bitalu_6_carryout), .RESULT(out_4[5]));  // open: SET
  _1bitALU u_1bitalu_7 (
    .A(in_2[6]), .B(b[6]), .LESS(1'b0), .A_INVERT(Inputs[3]), .BINVERT(Inputs[2]),
    .CARRY_IN(n1bitalu_6_carryout), .OPERATION(Inputs[1:0]), .CARRYOUT(n1bitalu_7_carryout), .RESULT(out_4[6]));  // open: SET
  _1bitALU u_1bitalu_8 (
    .A(in_2[7]), .B(b[7]), .LESS(1'b0), .A_INVERT(Inputs[3]), .BINVERT(Inputs[2]),
    .CARRY_IN(n1bitalu_7_carryout), .OPERATION(Inputs[1:0]), .CARRYOUT(Overflow), .RESULT(out_4[7]),
    .SET(n1bitalu_8_set));
  not not_1 (Zero, or_1_out);
  or or_1 (or_1_out, out_4[0], out_4[1], out_4[2], out_4[3], out_4[4], out_4[5], out_4[6], out_4[7]);

  // Notes on the sheet:
  //   a
  //   constant
  //   Result
endmodule
